# Fritzing sketch hardware ontwerp (saved by Fritzing 0.9.0b)
breadboards: 2

parts:
  Onderdeel1 = Arduino Uno (Rev3)
  LED1 = LED - 5mm [color="Red (633nm)" package="5 mm [THT]"]
  LED2 = LED - 5mm [color="Red (633nm)" package="5 mm [THT]"]
  LED3 = LED - 5mm [color="Red (633nm)" package="5 mm [THT]"]
  LED4 = LED - 5mm [color="Red (633nm)" package="5 mm [THT]"]
  LED5 = LED - 5mm [color="Red (633nm)" package="5 mm [THT]"]
  LED6 = LED - 5mm [color="Red (633nm)" package="5 mm [THT]"]
  LED7 = LED - 5mm [color="Red (633nm)" package="5 mm [THT]"]
  LED8 = LED - 5mm [color="Red (633nm)" package="5 mm [THT]"]
  R1 = Resistor [tolerance=±5% resistance=220 package=THT]
  R2 = Resistor [tolerance=±5% resistance=220 package=THT]
  R3 = Resistor [tolerance=±5% resistance=220 package=THT]
  R4 = Resistor [tolerance=±5% resistance=220 package=THT]
  R7 = Resistor [tolerance=±5% resistance=220 package=THT]
  R8 = Resistor [tolerance=±5% resistance=220 package=THT]
  R9 = Rotary Potentiometer (Small) [maximum_resistance=100kΩ package=THT]
  R10 = Resistor [tolerance=±5% resistance=220 package=THT]
  R11 = Photocell (LDR) [package=THT]
  R12 = Resistor [tolerance=±5% resistance=220 package=THT]
  C1 = Tantalum Capacitor [capacitance=1μF package="100 mil [THT, tantalum]"]
  R13 = Resistor [tolerance=±5% resistance=220 package=THT]
  S1 = Pushbutton [package="[THT]"]
  S2 = Pushbutton [package="[THT]"]
  S3 = Pushbutton [package="[THT]"]
  S4 = Pushbutton [package="[THT]"]
  R14 = Resistor [tolerance=±5% resistance=220 package=THT]
  R15 = Resistor [tolerance=±5% resistance=220 package=THT]
  R16 = Resistor [tolerance=±5% resistance=220 package=THT]
  R17 = Resistor [tolerance=±5% resistance=220 package=THT]
  R6 = Resistor [tolerance=±5% resistance=220 package=THT]
  R5 = Resistor [tolerance=±5% resistance=220 package=THT]

nets:
  N1: Onderdeel1.A0, C1.-, R13.Pin_1
  N2: Onderdeel1.A1, R11.pin_1
  N3: Onderdeel1.A2, R9.wiper
  N4: Onderdeel1.D8, LED2.anode
  N5: Onderdeel1.D9_PWM, LED1.anode
  N6: Onderdeel1.D10_PWM/SS, Onderdeel1.D11_PWM/MOSI, Onderdeel1.D12/MISO, Onderdeel1.D13/SCK, S1.Pin_1, S1.Pin_2, S2.Pin_1, S2.Pin_2, S3.Pin_1, S3.Pin_2, S4.Pin_1, S4.Pin_2
  N7: Onderdeel1.D2, LED8.anode
  N8: Onderdeel1.D3_PWM, LED7.anode
  N9: Onderdeel1.D4, LED6.anode
  N10: Onderdeel1.D5_PWM, LED5.anode
  N11: Onderdeel1.D6_PWM, LED4.anode
  N12: Onderdeel1.D7, LED3.anode
  N13: Onderdeel1.GND, R1.Pin_0, R2.Pin_0, R3.Pin_0, R4.Pin_0, R7.Pin_0, R8.Pin_0, C1.+, R6.Pin_0, R5.Pin_0
  N14: LED1.cathode, R1.Pin_1
  N15: LED2.cathode, R2.Pin_1
  N16: LED3.cathode, R3.Pin_1
  N17: LED4.cathode, R4.Pin_1
  N18: LED5.cathode, R8.Pin_1
  N19: LED6.cathode, R7.Pin_1
  N20: LED7.cathode, R6.Pin_1
  N21: LED8.cathode, R5.Pin_1
  N22: R9.leg2, R10.Pin_1
  N23: R11.pin_0, R12.Pin_0
  N24: S1.Pin_3, S1.Pin_4, R17.Pin_0
  N25: S2.Pin_3, S2.Pin_4, R16.Pin_0
  N26: S3.Pin_3, S3.Pin_4, R15.Pin_0
  N27: S4.Pin_3, S4.Pin_4, R14.Pin_0
  N28: R14.Pin_1, R15.Pin_1, R16.Pin_1, R17.Pin_1
